# Fritzing sketch Sketch (saved by Fritzing 0.9.3b)
breadboards: 1

parts:
  Componente1 = Bluetooth HM-10
  Componente2 = Arduino Uno (Rev3) - ICSP
  R1 = Resistor [tolerance=±5% resistance=1k package="0402 [SMD]"]
  R2 = Resistor [tolerance=±5% resistance=220 package="0402 [SMD]"]

nets:
  N1: Componente1.RXD, Componente2.D3_PWM, R1.Pin_1, R2.Pin_0
  N2: Componente1.TXD, Componente2.D2, R1.Pin_0
  GND: Componente1.GND, Componente2.GND, R2.Pin_1
  VCC: Componente1.VCC, Componente2.5V
